# Fritzing sketch smart home shema (saved by Fritzing 0.9.3b)
breadboards: 1

parts:
  R1 = Resistor [tolerance=±5% resistance=220 package=THT]
  R2 = Resistor [tolerance=±5% resistance=220 package=THT]
  LED1 = LED - 5mm [color="Red (633nm)" package="5 mm [THT]"]
  LED2 = LED - 5mm [color="Red (633nm)" package="5 mm [THT]"]
  FRDM-KL25Z1 = FRDM-KL25Z [part_number=FRDM-KL25Z]
  R3 = Resistor [tolerance=±5% resistance=220 package=THT]
  R4 = Photocell (LDR) [package=THT]
  T1 = LM35 Temperature Sensor [package="TO92 [THT]"]
  U1 = GAS_SENSOR [package=mq-3]
  U2 = MLX90614 [package=to-39]
  U3 = ESP8266 WiFi Module [part_number=ESP8266]

nets:
  N1: R1.Pin_0, R2.Pin_0, LED1.cathode, LED2.cathode, R4.pin_0, T1.GND, U1.B1, U2.SCL_VZ
  N2: R1.Pin_1, FRDM-KL25Z1.D8_PTA13
  N3: R2.Pin_1, FRDM-KL25Z1.D7_PTC9
  N4: FRDM-KL25Z1.A0_PTB0, U2.VDD
  N5: FRDM-KL25Z1.A2_PTB2, T1.Vout
  N6: FRDM-KL25Z1.A3_PTB3, R3.Pin_0, R4.pin_1
  N7: FRDM-KL25Z1.I2C_SDA_PTE0, U3.GPIO_14
  N8: FRDM-KL25Z1.I2C_SCL_PTE1, U3.GPIO_12
  GND: FRDM-KL25Z1.GND, FRDM-KL25Z1.GND2, U3.GPIO_13
  N9: FRDM-KL25Z1.P3V3, FRDM-KL25Z1.P3V3_2, R3.Pin_1
  N10: T1.+Vs, U1.A1, U2.PWM_SDA

custom parts:
  FRDM-KL25Z: Freedom Board, based on basic pinout of Arduino Rev.3. Attention: the board is NOT 5V compatible.
